# Fritzing sketch door (saved by Fritzing 0.9.3b)

parts:
  Part6 = NRF24L01+ Breakout Board
  Part7 = Arduino Nano (Rev3.0) (ICSP)
  J3 = Piezo Speaker
  S4 = Reed switch [package=THT]
  U2 = LIPO-110mAh [package=lipo-110]
  U3 = SWITCH_SPDT [package=kps-1290]

nets:
  GND: Part6.GND, Part7.GND, J3.pin1, S4.pin_2, U2.-
  VCC: Part6.VCC, Part7.3V3
  N1: Part6.CE, Part7.D7
  N2: Part6.CS, Part7.D8
  N3: Part6.SCK, Part7.D13/SCK
  N4: Part6.MOSI, Part7.D11/MOSI
  N5: Part6.MISO, Part7.D12/MISO
  N6: Part6.IRQ, Part7.D2
  N7: Part7.D3, S4.pin_1
  N8: Part7.D6, J3.pin2
  N9: Part7.VIN, U3.O
  N10: U2.+, U3.P
